// Logisim project CPU-v3.circ as structural Verilog
module half_adder (
  input  in_1,
  input  in_2,
  input  in_3,
  output out_4,
  output out_5
);

  wire and_1_out, and_2_out, xor_1_out;

  and and_1 (and_1_out, in_1, in_2);
  xor xor_1 (xor_1_out, in_2, in_1);
  and and_2 (and_2_out, in_3, xor_1_out);
  xor xor_2 (out_5, xor_1_out, in_3);
  or or_1 (out_4, and_1_out, and_2_out);
endmodule

module adder (
  input  B128,
  input  B64,
  input  B32,
  input  B16,
  input  B8,
  input  B4,
  input  B2,
  input  B1,
  input  A128,
  input  A64,
  input  A32,
  input  A16,
  input  A8,
  input  A4,
  input  A2,
  input  A,
  input  in_17,
  output out_18,
  output out_19,
  output out_20,
  output out_21,
  output out_22,
  output out_23,
  output out_24,
  output out_25,
  output out_26
);

  wire half_adder_2_out_4, half_adder_3_out_4, half_adder_4_out_4, half_adder_5_out_4, half_adder_6_out_4,
       half_adder_7_out_4, half_adder_8_out_4;

  half_adder half_adder_1 (.in_1(A128), .in_2(B128), .out_4(out_18), .in_3(half_adder_2_out_4), .out_5(out_19));
  half_adder half_adder_2 (
    .in_1(A64), .in_2(B64), .out_4(half_adder_2_out_4), .in_3(half_adder_3_out_4), .out_5(out_20));
  half_adder half_adder_3 (
    .in_1(A32), .in_2(B32), .out_4(half_adder_3_out_4), .in_3(half_adder_4_out_4), .out_5(out_21));
  half_adder half_adder_4 (
    .in_1(A16), .in_2(B16), .out_4(half_adder_4_out_4), .in_3(half_adder_5_out_4), .out_5(out_22));
  half_adder half_adder_5 (.in_1(A8), .in_2(B8), .out_4(half_adder_5_out_4), .in_3(half_adder_6_out_4), .out_5(out_23));
  half_adder half_adder_6 (.in_1(A4), .in_2(B4), .out_4(half_adder_6_out_4), .in_3(half_adder_7_out_4), .out_5(out_24));
  half_adder half_adder_7 (.in_1(A2), .in_2(B2), .out_4(half_adder_7_out_4), .in_3(half_adder_8_out_4), .out_5(out_25));
  half_adder half_adder_8 (.in_1(A), .in_2(B1), .out_4(half_adder_8_out_4), .in_3(in_17), .out_5(out_26));
endmodule

module UAL (
  input  B128,
  input  B64,
  input  B32,
  input  B16,
  input  B8,
  input  B4,
  input  B2,
  input  B1,
  input  A128,
  input  A64,
  input  A32,
  input  A16,
  input  A8,
  input  A4,
  input  A2,
  input  A,
  input  NOT,
  input  AND,
  input  XOR,
  input  ADD,
  input  ADD___CARRY_IN,
  input  SHL,
  input  _1,
  input  _2,
  input  _4,
  input  _8,
  input  SHR,
  output ZERO,
  output OVER_FLOW,
  output ODD,
  output _128,
  output _64,
  output _32,
  output _16,
  output _8_2,
  output _4_2,
  output _2_2,
  output _1_2
);

  wire adder_1_out_19, adder_1_out_20, adder_1_out_21, adder_1_out_22, adder_1_out_23, adder_1_out_24,
       adder_1_out_25, adder_1_out_26, and_1_out_17, and_1_out_18, and_1_out_19, and_1_out_20, and_1_out_21,
       and_1_out_22, and_1_out_23, and_1_out_24, demultiplexer_1_out1, demultiplexer_1_out2,
       demultiplexer_1_out3, demultiplexer_1_out4, demultiplexer_1_out5, demultiplexer_1_out6,
       demultiplexer_1_out7, demultiplexer_1_out8, demultiplexer_1_out9, gate_1_out_10, gate_1_out_11,
       gate_1_out_12, gate_1_out_13, gate_1_out_14, gate_1_out_15, gate_1_out_16, gate_1_out_17,
       gate_2_out_10, gate_2_out_11, gate_2_out_12, gate_2_out_13, gate_2_out_14, gate_2_out_15,
       gate_2_out_16, gate_2_out_17, gate_3_out_10, gate_3_out_11, gate_3_out_12, gate_3_out_13,
       gate_3_out_14, gate_3_out_15, gate_3_out_16, gate_3_out_17, gate_4_out_10, gate_4_out_11,
       gate_4_out_12, gate_4_out_13, gate_4_out_14, gate_4_out_15, gate_4_out_16, gate_4_out_17,
       inverteur_1_out_10, inverteur_1_out_11, inverteur_1_out_12, inverteur_1_out_13, inverteur_1_out_14,
       inverteur_1_out_15, inverteur_1_out_16, inverteur_1_out_17, or_1_out, or_2_out, or_3_out, or_4_out,
       or_8_out, SHL__2_2_out_10, SHL__2_2_out_11, SHL__2_2_out_12, SHL__2_2_out_13, SHL__2_2_out_14,
       SHL__2_2_out_15, SHL__2_2_out_16, SHL__2_2_out_17, SHL__2_out_10, SHL__2_out_11, SHL__2_out_12,
       SHL__2_out_13, SHL__2_out_14, SHL__2_out_15, SHL__2_out_16, SHL__2_out_17, xor_1_out_17, xor_1_out_18,
       xor_1_out_19, xor_1_out_20, xor_1_out_21, xor_1_out_22, xor_1_out_23, xor_1_out_24;

  Demultiplexer #(.select(4)) demultiplexer_1 (
    .out1(demultiplexer_1_out1), .out2(demultiplexer_1_out2), .out3(demultiplexer_1_out3),
    .out4(demultiplexer_1_out4), .out5(demultiplexer_1_out5), .out6(demultiplexer_1_out6),
    .out7(demultiplexer_1_out7), .out8(demultiplexer_1_out8), .out9(demultiplexer_1_out9), .in(1'b1),
    .sel({_8, _4, _2, _1}));  // open: out0, out10, out11, out12, out13, out14, out15, en
  adder adder_1 (
    .B128(B128), .B64(B64), .B32(B32), .B16(B16), .B8(B8), .B4(B4), .B2(B2), .B1(B1), .A128(A128), .A64(A64),
    .A32(A32), .A16(A16), .A8(A8), .A4(A4), .A2(A2), .A(A), .in_17(demultiplexer_1_out7), .out_18(OVER_FLOW),
    .out_19(adder_1_out_19), .out_20(adder_1_out_20), .out_21(adder_1_out_21), .out_22(adder_1_out_22),
    .out_23(adder_1_out_23), .out_24(adder_1_out_24), .out_25(adder_1_out_25), .out_26(adder_1_out_26));
  \and  and_1 (
    .B128(B128), .B64(B64), .B32(B32), .B16(B16), .B8(B8), .B4(B4), .B2(B2), .B1(B1), .A128(A128), .A64(A64),
    .A32(A32), .A16(A16), .A8(A8), .A4(A4), .A2(A2), .A(A), .out_17(and_1_out_17), .out_18(and_1_out_18),
    .out_19(and_1_out_19), .out_20(and_1_out_20), .out_21(and_1_out_21), .out_22(and_1_out_22),
    .out_23(and_1_out_23), .out_24(and_1_out_24));
  \xor  xor_1 (
    .B128(B128), .B64(B64), .B32(B32), .B16(B16), .B8(B8), .B4(B4), .B2(B2), .B1(B1), .A128(A128), .A64(A64),
    .A32(A32), .A16(A16), .A8(A8), .A4(A4), .A2(A2), .A(A), .out_17(xor_1_out_17), .out_18(xor_1_out_18),
    .out_19(xor_1_out_19), .out_20(xor_1_out_20), .out_21(xor_1_out_21), .out_22(xor_1_out_22),
    .out_23(xor_1_out_23), .out_24(xor_1_out_24));
  inverteur inverteur_1 (
    .A128(B128), .A64(B64), .A32(B32), .A16(B16), .A8(B8), .A4(B4), .A2(B2), .A(B1),
    .out_10(inverteur_1_out_10), .out_11(inverteur_1_out_11), .out_12(inverteur_1_out_12),
    .out_13(inverteur_1_out_13), .out_14(inverteur_1_out_14), .out_15(inverteur_1_out_15),
    .out_16(inverteur_1_out_16), .out_17(inverteur_1_out_17), .PASS(demultiplexer_1_out2));
  or or_1 (or_1_out, demultiplexer_1_out7, demultiplexer_1_out6);
  gate gate_1 (
    .A128(adder_1_out_19), .A64(adder_1_out_20), .A32(adder_1_out_21), .A16(adder_1_out_22),
    .A8(adder_1_out_23), .A4(adder_1_out_24), .A2(adder_1_out_25), .A(adder_1_out_26), .PASS(or_1_out),
    .out_10(gate_1_out_10), .out_11(gate_1_out_11), .out_12(gate_1_out_12), .out_13(gate_1_out_13),
    .out_14(gate_1_out_14), .out_15(gate_1_out_15), .out_16(gate_1_out_16), .out_17(gate_1_out_17));
  gate gate_2 (
    .A128(and_1_out_17), .A64(and_1_out_18), .A32(and_1_out_19), .A16(and_1_out_20), .A8(and_1_out_21),
    .A4(and_1_out_22), .A2(and_1_out_23), .A(and_1_out_24), .PASS(or_2_out), .out_10(gate_2_out_10),
    .out_11(gate_2_out_11), .out_12(gate_2_out_12), .out_13(gate_2_out_13), .out_14(gate_2_out_14),
    .out_15(gate_2_out_15), .out_16(gate_2_out_16), .out_17(gate_2_out_17));
  gate gate_3 (
    .A128(xor_1_out_17), .A64(xor_1_out_18), .A32(xor_1_out_19), .A16(xor_1_out_20), .A8(xor_1_out_21),
    .A4(xor_1_out_22), .A2(xor_1_out_23), .A(xor_1_out_24), .PASS(or_3_out), .out_10(gate_3_out_10),
    .out_11(gate_3_out_11), .out_12(gate_3_out_12), .out_13(gate_3_out_13), .out_14(gate_3_out_14),
    .out_15(gate_3_out_15), .out_16(gate_3_out_16), .out_17(gate_3_out_17));
  gate gate_4 (
    .A128(inverteur_1_out_10), .A64(inverteur_1_out_11), .A32(inverteur_1_out_12), .A16(inverteur_1_out_13),
    .A8(inverteur_1_out_14), .A4(inverteur_1_out_15), .A2(inverteur_1_out_16), .A(inverteur_1_out_17),
    .PASS(or_4_out), .out_10(gate_4_out_10), .out_11(gate_4_out_11), .out_12(gate_4_out_12),
    .out_13(gate_4_out_13), .out_14(gate_4_out_14), .out_15(gate_4_out_15), .out_16(gate_4_out_16),
    .out_17(gate_4_out_17));
  or or_2 (or_2_out, demultiplexer_1_out3, demultiplexer_1_out5);
  or or_3 (or_3_out, demultiplexer_1_out5, demultiplexer_1_out4);
  or or_4 (or_4_out, demultiplexer_1_out1, demultiplexer_1_out2);
  or or_5 (_128, gate_1_out_10, gate_2_out_10, gate_3_out_10, gate_4_out_10, SHL__2_out_10, SHL__2_2_out_10);
  gate SHL__2 (
    .A128(1'b0), .A64(B128), .A32(B64), .A16(B32), .A8(B16), .A4(B8), .A2(B4), .A(B2),
    .PASS(demultiplexer_1_out8), .out_10(SHL__2_out_10), .out_11(SHL__2_out_11), .out_12(SHL__2_out_12),
    .out_13(SHL__2_out_13), .out_14(SHL__2_out_14), .out_15(SHL__2_out_15), .out_16(SHL__2_out_16),
    .out_17(SHL__2_out_17));
  gate SHL__2_2 (
    .A128(B64), .A64(B32), .A32(B16), .A16(B8), .A8(B4), .A4(B2), .A2(B1), .A(1'b0),
    .PASS(demultiplexer_1_out9), .out_10(SHL__2_2_out_10), .out_11(SHL__2_2_out_11),
    .out_12(SHL__2_2_out_12), .out_13(SHL__2_2_out_13), .out_14(SHL__2_2_out_14), .out_15(SHL__2_2_out_15),
    .out_16(SHL__2_2_out_16), .out_17(SHL__2_2_out_17));
  or or_6 (_64, gate_1_out_11, gate_2_out_11, gate_3_out_11, gate_4_out_11, SHL__2_out_11, SHL__2_2_out_11);
  or or_7 (_32, gate_1_out_12, gate_2_out_12, gate_3_out_12, gate_4_out_12, SHL__2_out_12, SHL__2_2_out_12);
  or or_8 (or_8_out, _128, _64, _32, _16, _8_2, _4_2, _2_2, _1_2);
  or or_9 (_16, gate_1_out_13, gate_2_out_13, gate_3_out_13, gate_4_out_13, SHL__2_out_13, SHL__2_2_out_13);
  or or_10 (_8_2, gate_1_out_14, gate_2_out_14, gate_3_out_14, gate_4_out_14, SHL__2_out_14, SHL__2_2_out_14);
  or or_11 (_4_2, gate_1_out_15, gate_2_out_15, gate_3_out_15, gate_4_out_15, SHL__2_out_15, SHL__2_2_out_15);
  or or_12 (_2_2, gate_1_out_16, gate_2_out_16, gate_3_out_16, gate_4_out_16, SHL__2_out_16, SHL__2_2_out_16);
  not not_1 (ZERO, or_8_out);
  or or_13 (_1_2, gate_1_out_17, gate_2_out_17, gate_3_out_17, gate_4_out_17, SHL__2_out_17, SHL__2_2_out_17);

  assign ODD = _1_2;
endmodule

module \and  (
  input  B128,
  input  B64,
  input  B32,
  input  B16,
  input  B8,
  input  B4,
  input  B2,
  input  B1,
  input  A128,
  input  A64,
  input  A32,
  input  A16,
  input  A8,
  input  A4,
  input  A2,
  input  A,
  output out_17,
  output out_18,
  output out_19,
  output out_20,
  output out_21,
  output out_22,
  output out_23,
  output out_24
);

  and and_1 (out_17, B128, A128);
  and and_2 (out_18, B64, A64);
  and and_3 (out_19, B32, A32);
  and and_4 (out_20, B16, A16);
  and and_5 (out_21, B8, A8);
  and and_6 (out_22, B4, A4);
  and and_7 (out_23, B2, A2);
  and and_8 (out_24, B1, A);
endmodule

module \xor  (
  input  B128,
  input  B64,
  input  B32,
  input  B16,
  input  B8,
  input  B4,
  input  B2,
  input  B1,
  input  A128,
  input  A64,
  input  A32,
  input  A16,
  input  A8,
  input  A4,
  input  A2,
  input  A,
  output out_17,
  output out_18,
  output out_19,
  output out_20,
  output out_21,
  output out_22,
  output out_23,
  output out_24
);

  xor xor_1 (out_17, B128, A128);
  xor xor_2 (out_18, B64, A64);
  xor xor_3 (out_19, B32, A32);
  xor xor_4 (out_20, B16, A16);
  xor xor_5 (out_21, B8, A8);
  xor xor_6 (out_22, B4, A4);
  xor xor_7 (out_23, B2, A2);
  xor xor_8 (out_24, B1, A);
endmodule

module gate (
  input  A128,
  input  A64,
  input  A32,
  input  A16,
  input  A8,
  input  A4,
  input  A2,
  input  A,
  input  PASS,
  output out_10,
  output out_11,
  output out_12,
  output out_13,
  output out_14,
  output out_15,
  output out_16,
  output out_17
);

  and and_1 (out_10, A128, PASS);
  and and_2 (out_11, A64, PASS);
  and and_3 (out_12, A32, PASS);
  and and_4 (out_13, A16, PASS);
  and and_5 (out_14, A8, PASS);
  and and_6 (out_15, A4, PASS);
  and and_7 (out_16, A2, PASS);
  and and_8 (out_17, A, PASS);
endmodule

module inverteur (
  input  A128,
  input  A64,
  input  A32,
  input  A16,
  input  A8,
  input  A4,
  input  A2,
  input  A,
  input  PASS,
  output out_10,
  output out_11,
  output out_12,
  output out_13,
  output out_14,
  output out_15,
  output out_16,
  output out_17
);

  xor xor_1 (out_10, A128, PASS);
  xor xor_2 (out_11, A64, PASS);
  xor xor_3 (out_12, A32, PASS);
  xor xor_4 (out_13, A16, PASS);
  xor xor_5 (out_14, A8, PASS);
  xor xor_6 (out_15, A4, PASS);
  xor xor_7 (out_16, A2, PASS);
  xor xor_8 (out_17, A, PASS);
endmodule

module CPU (
  input  [7:0] in_1,
  input  TICK_ONCE,
  input  ENABLE_CLOCK,
  output [7:0] OUTPUT,
  output [7:0] RAM,
  output STORE,
  output [2:0] WRITE_ON,
  output [2:0] REG_A,
  output [2:0] REG_B,
  output CUT_A,
  output CUT_B,
  output [3:0] ALU,
  output [2:0] FLAG,
  output [4:0] OTHER
);

  wire and_1_out, and_2_out, and_3_out, and_4_out, and_5_out, clock_1_out, decoder_1_out0, decoder_1_out1,
       decoder_1_out2, decoder_1_out3, decoder_1_out4, decoder_1_out5, decoder_1_out6, decoder_1_out7,
       decoder_2_out0, decoder_2_out1, decoder_3_out1, decoder_3_out3, decoder_4_out1, decoder_4_out2,
       decoder_4_out3, decoder_4_out4, decoder_5_out1, decoder_5_out2, decoder_5_out3, decoder_5_out4,
       decoder_5_out5, not_1_out, not_2_out, not_3_out, not_4_out, not_5_out, ODD_q, or_3_out, or_5_out,
       or_6_out, OVERFLOW_q, ual_1_odd, ual_1_over_flow, ual_1_zero, ZERO_q;
  wire [7:0] controlled_buffer_2_out, controlled_buffer_3_out, counter_1_q, gate_8bits_1_out_3,
       multiplexer_1_out, multiplexer_2_out, or_1_out, or_2_out, or_4_out, ram_1_data, register_1_q,
       register_2_q, register_3_q, register_4_q, register_5_q, register_6_q, register_7_q, register_8_q;
  wire [15:0] gpu_1_output, gpu_1_output_2, gpu_1_output_3, gpu_1_output_4, gpu_1_output_5, gpu_1_output_6,
       gpu_1_output_7, gpu_1_output_8, gpu_1_output_9, gpu_1_output_10, gpu_1_output_11, gpu_1_output_12,
       gpu_1_output_13, gpu_1_output_14, gpu_1_output_15, gpu_1_output_16;

  assign or_1_out = RAM | gate_8bits_1_out_3;  // OR_Gate or_1, 8 bits wide
  and and_1 (and_1_out, ENABLE_CLOCK, clock_1_out);
  Clock clock_1 (.out(clock_1_out));
  assign or_2_out = ram_1_data | or_4_out;  // OR_Gate or_2, 8 bits wide
  Decoder #(.select(3)) decoder_1 (
    .out0(decoder_1_out0), .out1(decoder_1_out1), .out2(decoder_1_out2), .out3(decoder_1_out3),
    .out4(decoder_1_out4), .out5(decoder_1_out5), .out6(decoder_1_out6), .out7(decoder_1_out7), .sel(WRITE_ON));  // open: en
  not not_1 (not_1_out, decoder_3_out3);
  or or_3 (or_3_out, TICK_ONCE, and_1_out);
  Register register_1 (.D(or_2_out), .en(decoder_1_out0), .Q(register_1_q), .clk(not_2_out));  // open: clr
  Register register_2 (.D(or_2_out), .en(decoder_1_out1), .Q(register_2_q), .clk(not_2_out));  // open: clr
  Register register_3 (.D(or_2_out), .en(decoder_1_out2), .Q(register_3_q), .clk(not_2_out));  // open: clr
  Register register_4 (.D(or_2_out), .en(decoder_1_out3), .Q(register_4_q), .clk(not_2_out));  // open: clr
  Register register_5 (.D(or_2_out), .en(decoder_1_out4), .Q(register_5_q), .clk(not_2_out));  // open: clr
  Register register_6 (.D(or_2_out), .en(decoder_1_out5), .Q(register_6_q), .clk(not_2_out));  // open: clr
  Register register_7 (.D(or_2_out), .en(decoder_1_out6), .Q(register_7_q), .clk(not_2_out));  // open: clr
  Register register_8 (.D(or_2_out), .en(decoder_1_out7), .Q(register_8_q), .clk(not_2_out));  // open: clr
  not not_2 (not_2_out, and_2_out);
  Decoder decoder_2 (.out0(decoder_2_out0), .out1(decoder_2_out1), .sel(or_6_out));  // open: en
  and and_2 (and_2_out, not_1_out, or_3_out);
  RAM ram_1 (.addr(or_1_out), .data(ram_1_data), .clk(not_2_out), .ld(not_3_out));  // open: sel, clr
  not not_3 (not_3_out, STORE);
  assign ram_1_data = STORE ? or_4_out : 8'bz;  // Controlled_Buffer controlled_buffer_1
  assign or_4_out = in_1 | OUTPUT;  // OR_Gate or_4, 8 bits wide
  Gate_8bits gate_8bits_1 (.A(register_8_q), .A_2(decoder_3_out1), .out_3(gate_8bits_1_out_3));
  Decoder #(.select(2)) decoder_3 (
    .out1(decoder_3_out1), .out3(decoder_3_out3), .sel(OTHER[4:3]));  // open: out0, out2, en
  Counter counter_1 (
    .load(decoder_2_out1), .D(RAM), .count(decoder_2_out0), .Q(counter_1_q), .clk(and_2_out));  // open: carry, clr
  Multiplexer #(.select(3), .width(8)) multiplexer_1 (
    .in0(register_1_q), .in1(register_2_q), .in2(register_3_q), .in3(register_4_q), .in4(register_5_q),
    .in5(register_6_q), .in6(register_7_q), .in7(register_8_q), .out(multiplexer_1_out), .sel(REG_B));  // open: en
  assign controlled_buffer_2_out = not_4_out ? multiplexer_1_out : 8'bz;  // Controlled_Buffer controlled_buffer_2
  not not_4 (not_4_out, CUT_B);
  Multiplexer #(.select(3), .width(8)) multiplexer_2 (
    .in0(register_1_q), .in1(register_2_q), .in2(register_3_q), .in3(register_4_q), .in4(register_5_q),
    .in5(register_6_q), .in6(register_7_q), .in7(register_8_q), .out(multiplexer_2_out), .sel(REG_A));  // open: en
  assign controlled_buffer_3_out = not_5_out ? multiplexer_2_out : 8'bz;  // Controlled_Buffer controlled_buffer_3
  not not_5 (not_5_out, CUT_A);
  ROM #(.dataWidth(32)) rom_1 (
    .addr(counter_1_q), .data({OTHER, FLAG, ALU, CUT_B, CUT_A, REG_B, REG_A, WRITE_ON, STORE, RAM}),
    .sel(1'b1));
  DotMatrix #(.matrixcols(16), .matrixrows(16)) dotmatrix_1 (
    .col0(gpu_1_output), .col1(gpu_1_output_2), .col2(gpu_1_output_3), .col3(gpu_1_output_4),
    .col4(gpu_1_output_5), .col5(gpu_1_output_6), .col6(gpu_1_output_7), .col7(gpu_1_output_8),
    .col8(gpu_1_output_9), .col9(gpu_1_output_10), .col10(gpu_1_output_11), .col11(gpu_1_output_12),
    .col12(gpu_1_output_13), .col13(gpu_1_output_14), .col14(gpu_1_output_15), .col15(gpu_1_output_16));
  GPU gpu_1 (
    .CLOCK(not_2_out), .OUTPUT(gpu_1_output), .OUTPUT_2(gpu_1_output_2), .OUTPUT_3(gpu_1_output_3),
    .OUTPUT_4(gpu_1_output_4), .OUTPUT_5(gpu_1_output_5), .OUTPUT_6(gpu_1_output_6),
    .OUTPUT_7(gpu_1_output_7), .OUTPUT_8(gpu_1_output_8), .OUTPUT_9(gpu_1_output_9),
    .OUTPUT_10(gpu_1_output_10), .OUTPUT_11(gpu_1_output_11), .OUTPUT_12(gpu_1_output_12),
    .OUTPUT_13(gpu_1_output_13), .OUTPUT_14(gpu_1_output_14), .OUTPUT_15(gpu_1_output_15),
    .OUTPUT_16(gpu_1_output_16), .Y(or_4_out), .X(or_4_out), .SAVE_X(decoder_4_out1),
    .SAVE_Y(decoder_4_out2), .DRAW(decoder_4_out3), .RESET(decoder_4_out4));
  UAL ual_1 (
    .B128(controlled_buffer_2_out[7]), .B64(controlled_buffer_2_out[6]), .B32(controlled_buffer_2_out[5]),
    .B16(controlled_buffer_2_out[4]), .B8(controlled_buffer_2_out[3]), .B4(controlled_buffer_2_out[2]),
    .B2(controlled_buffer_2_out[1]), .B1(controlled_buffer_2_out[0]), .A128(controlled_buffer_3_out[7]),
    .A64(controlled_buffer_3_out[6]), .A32(controlled_buffer_3_out[5]), .A16(controlled_buffer_3_out[4]),
    .A8(controlled_buffer_3_out[3]), .A4(controlled_buffer_3_out[2]), .A2(controlled_buffer_3_out[1]),
    .A(controlled_buffer_3_out[0]), .ZERO(ual_1_zero), .OVER_FLOW(ual_1_over_flow), .ODD(ual_1_odd),
    ._128(OUTPUT[7]), ._64(OUTPUT[6]), ._32(OUTPUT[5]), ._16(OUTPUT[4]), ._8_2(OUTPUT[3]), ._4_2(OUTPUT[2]),
    ._2_2(OUTPUT[1]), ._1_2(OUTPUT[0]), ._1(ALU[0]), ._2(ALU[1]), ._4(ALU[2]), ._8(ALU[3]));  // open: NOT, AND, XOR, ADD, ADD___CARRY_IN, SHL, SHR
  Register #(.width(1)) ZERO (.D(ual_1_zero), .en(decoder_5_out1), .Q(ZERO_q), .clk(not_2_out));  // open: clr
  Decoder #(.select(3)) decoder_4 (
    .out1(decoder_4_out1), .out2(decoder_4_out2), .out3(decoder_4_out3), .out4(decoder_4_out4),
    .sel(OTHER[2:0]));  // open: out0, out5, out6, out7, en
  Register #(.width(1)) OVERFLOW (
    .D(ual_1_over_flow), .en(decoder_5_out1), .Q(OVERFLOW_q), .clk(not_2_out));  // open: clr
  Register #(.width(1)) ODD (.D(ual_1_odd), .en(decoder_5_out1), .Q(ODD_q), .clk(not_2_out));  // open: clr
  Decoder #(.select(3)) decoder_5 (
    .out1(decoder_5_out1), .out2(decoder_5_out2), .out3(decoder_5_out3), .out4(decoder_5_out4),
    .out5(decoder_5_out5), .sel(FLAG));  // open: out0, out6, out7, en
  and and_3 (and_3_out, ZERO_q, decoder_5_out2);
  and and_4 (and_4_out, OVERFLOW_q, decoder_5_out3);
  and and_5 (and_5_out, ODD_q, decoder_5_out4);
  or or_5 (or_5_out, and_5_out, and_4_out, and_3_out);
  or or_6 (or_6_out, decoder_5_out5, or_5_out);

  // Notes on the sheet:
  //   REG
  //   contents of rom_1 (hex, n*v repeats v):
  //   0 201 402 727e00 0 1611400 300000f 10150000 8178000 18000000 40150100 73ee00 45000004 0 0 0 c0000000
  //   FLAGS
endmodule

module Gate_8bits (
  input  [7:0] A,
  input  A_2,
  output [7:0] out_3
);

  gate gate_1 (
    .A128(A[0]), .A64(A[1]), .A32(A[2]), .A16(A[3]), .A8(A[4]), .A4(A[5]), .A2(A[6]), .A(A[7]), .PASS(A_2),
    .out_10(out_3[0]), .out_11(out_3[1]), .out_12(out_3[2]), .out_13(out_3[3]), .out_14(out_3[4]),
    .out_15(out_3[5]), .out_16(out_3[6]), .out_17(out_3[7]));
endmodule

module reg_Y_axes (
  input  [7:0] A,
  input  CLOCK,
  input  RESET,
  output [15:0] OUTPUT
);

  wire decoder_1_out0, decoder_1_out1, decoder_1_out2, decoder_1_out3, decoder_1_out4, decoder_1_out5,
       decoder_1_out6, decoder_1_out7, decoder_1_out8, decoder_1_out9, decoder_1_out10, decoder_1_out11,
       decoder_1_out12, decoder_1_out13, decoder_1_out14, decoder_1_out15;

  Decoder #(.select(4)) decoder_1 (
    .out0(decoder_1_out0), .out1(decoder_1_out1), .out2(decoder_1_out2), .out3(decoder_1_out3),
    .out4(decoder_1_out4), .out5(decoder_1_out5), .out6(decoder_1_out6), .out7(decoder_1_out7),
    .out8(decoder_1_out8), .out9(decoder_1_out9), .out10(decoder_1_out10), .out11(decoder_1_out11),
    .out12(decoder_1_out12), .out13(decoder_1_out13), .out14(decoder_1_out14), .out15(decoder_1_out15),
    .sel(A[3:0]));  // open: en
  Register #(.width(1)) register_1 (.D(1'b1), .en(decoder_1_out0), .Q(OUTPUT[0]), .clk(CLOCK), .clr(RESET));
  Register #(.width(1)) register_2 (.D(1'b1), .en(decoder_1_out1), .Q(OUTPUT[1]), .clk(CLOCK), .clr(RESET));
  Register #(.width(1)) register_3 (.D(1'b1), .en(decoder_1_out2), .Q(OUTPUT[2]), .clk(CLOCK), .clr(RESET));
  Register #(.width(1)) register_4 (.D(1'b1), .en(decoder_1_out3), .Q(OUTPUT[3]), .clk(CLOCK), .clr(RESET));
  Register #(.width(1)) register_5 (.D(1'b1), .en(decoder_1_out4), .Q(OUTPUT[4]), .clk(CLOCK), .clr(RESET));
  Register #(.width(1)) register_6 (.D(1'b1), .en(decoder_1_out5), .Q(OUTPUT[5]), .clk(CLOCK), .clr(RESET));
  Register #(.width(1)) register_7 (.D(1'b1), .en(decoder_1_out6), .Q(OUTPUT[6]), .clk(CLOCK), .clr(RESET));
  Register #(.width(1)) register_8 (.D(1'b1), .en(decoder_1_out7), .Q(OUTPUT[7]), .clk(CLOCK), .clr(RESET));
  Register #(.width(1)) register_9 (.D(1'b1), .en(decoder_1_out8), .Q(OUTPUT[8]), .clk(CLOCK), .clr(RESET));
  Register #(.width(1)) register_10 (.D(1'b1), .en(decoder_1_out9), .Q(OUTPUT[9]), .clk(CLOCK), .clr(RESET));
  Register #(.width(1)) register_11 (.D(1'b1), .en(decoder_1_out10), .Q(OUTPUT[10]), .clk(CLOCK), .clr(RESET));
  Register #(.width(1)) register_12 (.D(1'b1), .en(decoder_1_out11), .Q(OUTPUT[11]), .clk(CLOCK), .clr(RESET));
  Register #(.width(1)) register_13 (.D(1'b1), .en(decoder_1_out12), .Q(OUTPUT[12]), .clk(CLOCK), .clr(RESET));
  Register #(.width(1)) register_14 (.D(1'b1), .en(decoder_1_out13), .Q(OUTPUT[13]), .clk(CLOCK), .clr(RESET));
  Register #(.width(1)) register_15 (.D(1'b1), .en(decoder_1_out14), .Q(OUTPUT[14]), .clk(CLOCK), .clr(RESET));
  Register #(.width(1)) register_16 (.D(1'b1), .en(decoder_1_out15), .Q(OUTPUT[15]), .clk(CLOCK), .clr(RESET));
endmodule

module GPU (
  input  CLOCK,
  input  DRAW,
  input  RESET,
  input  [7:0] Y,
  input  [7:0] X,
  input  SAVE_X,
  input  SAVE_Y,
  output [15:0] OUTPUT,
  output [15:0] OUTPUT_2,
  output [15:0] OUTPUT_3,
  output [15:0] OUTPUT_4,
  output [15:0] OUTPUT_5,
  output [15:0] OUTPUT_6,
  output [15:0] OUTPUT_7,
  output [15:0] OUTPUT_8,
  output [15:0] OUTPUT_9,
  output [15:0] OUTPUT_10,
  output [15:0] OUTPUT_11,
  output [15:0] OUTPUT_12,
  output [15:0] OUTPUT_13,
  output [15:0] OUTPUT_14,
  output [15:0] OUTPUT_15,
  output [15:0] OUTPUT_16
);

  wire [3:0] not_1_out, register_2_q;
  wire [7:0] demultiplexer_1_out0, demultiplexer_1_out1, demultiplexer_1_out2, demultiplexer_1_out3,
       demultiplexer_1_out4, demultiplexer_1_out5, demultiplexer_1_out6, demultiplexer_1_out7,
       demultiplexer_1_out8, demultiplexer_1_out9, demultiplexer_1_out10, demultiplexer_1_out11,
       demultiplexer_1_out12, demultiplexer_1_out13, demultiplexer_1_out14, demultiplexer_1_out15,
       register_1_q;

  Register register_1 (.D(Y), .en(SAVE_Y), .Q(register_1_q), .clk(CLOCK));  // open: clr
  Register #(.width(4)) register_2 (.D(X[3:0]), .en(SAVE_X), .Q(register_2_q), .clk(CLOCK));  // open: clr
  Demultiplexer #(.select(4), .width(8)) demultiplexer_1 (
    .out0(demultiplexer_1_out0), .out1(demultiplexer_1_out1), .out2(demultiplexer_1_out2),
    .out3(demultiplexer_1_out3), .out4(demultiplexer_1_out4), .out5(demultiplexer_1_out5),
    .out6(demultiplexer_1_out6), .out7(demultiplexer_1_out7), .out8(demultiplexer_1_out8),
    .out9(demultiplexer_1_out9), .out10(demultiplexer_1_out10), .out11(demultiplexer_1_out11),
    .out12(demultiplexer_1_out12), .out13(demultiplexer_1_out13), .out14(demultiplexer_1_out14),
    .out15(demultiplexer_1_out15), .in(register_1_q), .sel(not_1_out));  // open: en
  assign not_1_out = ~register_2_q;  // NOT_Gate not_1, 4 bits wide
  reg_Y_axes reg_y_axes_1 (.A(demultiplexer_1_out14), .OUTPUT(OUTPUT_2), .CLOCK(DRAW), .RESET(RESET));
  reg_Y_axes reg_y_axes_2 (.A(demultiplexer_1_out15), .OUTPUT(OUTPUT), .CLOCK(DRAW), .RESET(RESET));
  reg_Y_axes reg_y_axes_3 (.A(demultiplexer_1_out12), .OUTPUT(OUTPUT_4), .CLOCK(DRAW), .RESET(RESET));
  reg_Y_axes reg_y_axes_4 (.A(demultiplexer_1_out13), .OUTPUT(OUTPUT_3), .CLOCK(DRAW), .RESET(RESET));
  reg_Y_axes reg_y_axes_5 (.A(demultiplexer_1_out10), .OUTPUT(OUTPUT_6), .CLOCK(DRAW), .RESET(RESET));
  reg_Y_axes reg_y_axes_6 (.A(demultiplexer_1_out11), .OUTPUT(OUTPUT_5), .CLOCK(DRAW), .RESET(RESET));
  reg_Y_axes reg_y_axes_7 (.A(demultiplexer_1_out8), .OUTPUT(OUTPUT_8), .CLOCK(DRAW), .RESET(RESET));
  reg_Y_axes reg_y_axes_8 (.A(demultiplexer_1_out9), .OUTPUT(OUTPUT_7), .CLOCK(DRAW), .RESET(RESET));
  reg_Y_axes reg_y_axes_9 (.A(demultiplexer_1_out6), .OUTPUT(OUTPUT_10), .CLOCK(DRAW), .RESET(RESET));
  reg_Y_axes reg_y_axes_10 (.A(demultiplexer_1_out7), .OUTPUT(OUTPUT_9), .CLOCK(DRAW), .RESET(RESET));
  reg_Y_axes reg_y_axes_11 (.A(demultiplexer_1_out4), .OUTPUT(OUTPUT_12), .CLOCK(DRAW), .RESET(RESET));
  reg_Y_axes reg_y_axes_12 (.A(demultiplexer_1_out5), .OUTPUT(OUTPUT_11), .CLOCK(DRAW), .RESET(RESET));
  reg_Y_axes reg_y_axes_13 (.A(demultiplexer_1_out2), .OUTPUT(OUTPUT_14), .CLOCK(DRAW), .RESET(RESET));
  reg_Y_axes reg_y_axes_14 (.A(demultiplexer_1_out3), .OUTPUT(OUTPUT_13), .CLOCK(DRAW), .RESET(RESET));
  reg_Y_axes reg_y_axes_15 (.A(demultiplexer_1_out0), .OUTPUT(OUTPUT_16), .CLOCK(DRAW), .RESET(RESET));
  reg_Y_axes reg_y_axes_16 (.A(demultiplexer_1_out1), .OUTPUT(OUTPUT_15), .CLOCK(DRAW), .RESET(RESET));
endmodule
